# Fritzing sketch Demo2kytkenta (saved by Fritzing 0.9.3b)
breadboards: 1

parts:
  R1 = Resistor [tolerance=±5% resistance=220 package=THT]
  Part1 = Adafruit T-Cobbler Plus [part_number="Adafruit #1989 and #2028"]
  LED1 = LED - 5mm [color="Red (633nm)" package="5 mm [THT]"]
  LED2 = LED - 5mm [color="Red (633nm)" package="5 mm [THT]"]
  LED3 = LED - 5mm [color="Yellow (595nm)" package="5 mm [THT]"]
  LED4 = LED - 5mm [color="Green (555nm)" package="5 mm [THT]"]
  LED5 = LED - 5mm [color="Yellow (595nm)" package="5 mm [THT]"]
  LED6 = LED - 5mm [color="Green (555nm)" package="5 mm [THT]"]
  R2 = Resistor [tolerance=±5% resistance=220 package=THT]
  R3 = Resistor [tolerance=±5% resistance=220 package=THT]
  R4 = Resistor [tolerance=±5% resistance=220 package=THT]
  R5 = Resistor [tolerance=±5% resistance=220 package=THT]
  R6 = Resistor [tolerance=±5% resistance=220 package=THT]
  R7 = Resistor [tolerance=±5% resistance=220 package=THT]
  S1 = Pushbutton [package="[THT]"]
  U1 = MLX90614 [package=to-39]

nets:
  N1: R1.Pin_0, Part1.GPIO19, S1.Pin_1, S1.Pin_2
  N2: R1.Pin_1, Part1.GND, R2.Pin_1, R3.Pin_0, R4.Pin_1, R5.Pin_0, R6.Pin_1, R7.Pin_0, U1.SCL_VZ
  N3: Part1.+3.3V_2, S1.Pin_3, S1.Pin_4
  N4: Part1.GPIO5, LED1.anode
  N5: Part1.GPIO6, LED6.anode
  N6: Part1.GPIO13, LED5.anode
  N7: Part1.+5V, U1.PWM_SDA
  N8: Part1.GPIO25, LED4.anode
  N9: Part1.GPIO16, LED2.anode
  N10: Part1.GPIO20, LED3.anode
  N11: LED1.cathode, R2.Pin_0
  N12: LED2.cathode, R5.Pin_1
  N13: LED3.cathode, R6.Pin_0
  N14: LED4.cathode, R7.Pin_1
  N15: LED5.cathode, R4.Pin_0
  N16: LED6.cathode, R3.Pin_1

custom parts:
  Adafruit T-Cobbler Plus: The Raspberry Pi has landed on the Maker World like a 40-GPIO pinned, quad-USB ported, credit card sized bomb of DIY joy. And while you can use most of our great Model B accessories by hooking up our downgrade cable, its probably a good time to upgrade your set up and accessorize using all of the 40 pins. That's why we now carry the Assembled Adafruit Pi T-Cobbler Plus - Breakout + Cable for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
